// Digital circuit max2.dig as structural Verilog
module max2 (
  input  [1:0] a0,
  input  [1:0] b0,
  input  [1:0] a1,
  input  [1:0] b1,
  output [1:0] r0,
  output [1:0] r1
);

  assign r0 = a0 | b0;  // Or or_1, 2 bits wide
  assign r1 = a1 | b1;  // Or or_2, 2 bits wide
endmodule
